# Fritzing sketch Arduino MEGA 2 moteurs (saved by Fritzing 0.9.3b)

parts:
  Composant1 = Arduino Mega ADK (Rev3)  # not connected
  Mod2 = TMC2209 [package=THT]
  Mod3 = TMC2209 [package=THT]
  M3 = RAMPS_1.4
  M1 = Stepper Motor - Bipolar
  M2 = Stepper Motor - Bipolar
  Power_plug1 = Power plug
  R1 = Resistor [tolerance=±5% resistance=1k package="0402 [SMD]"]
  R2 = Resistor [tolerance=±5% resistance=1k package="0402 [SMD]"]

nets:
  N1: Mod2.PDN2, M3.E0-MS3, M3.D15/Y-MAX, R1.Pin_0
  N2: Mod3.PDN2, M3.D19/Z-MAX, R2.Pin_0
  N3: M3.E0-2B, M1.A
  N4: M3.E0-2A, M1.C
  N5: M3.E0-1A, M1.B
  N6: M3.E0-1B, M1.D
  N7: M3.E1-2B, M2.A
  N8: M3.E1-2A, M2.C
  N9: M3.E1-1A, M2.B
  N10: M3.E1-1B, M2.D
  N11: M3.D14/Y-MIN, R1.Pin_1
  N12: M3.D18/Z-MIN, R2.Pin_1
  GND: M3.GND, Power_plug1.GND
  +12V: M3.+12V, Power_plug1.VCC

notes:
  Alimentation 12V 5A
  RA
  DC

custom parts:
  TMC2209: TMC2209-LA stepper motor controller and driver. Supply voltage 4.75-28V Iphase up to 1.77A rms (2.5A peak)
  RAMPS_1.4: Ramps 1.4 3d printer driver module. Pcb view has been supressed as not useful. Note you can drag the A4988 stepper controller over the sockets on the card and they will connect correctly (there is currently a Fritzing bug which will say there are connections unrouted however). At present the mega connections are not populated, although with work on schematic that could be done too.
